// Logisim project aaa.circ as structural Verilog: 1 circuit, main circuit main
module main (
);

  wire and_1_out, and_2_out, and_3_out, and_4_out, and_5_out, and_6_out, and_7_out, and_8_out, and_9_out,
       and_10_out, and_11_out, and_12_out, and_13_out, and_14_out, or_1_out, or_2_out, or_3_out, or_4_out,
       undriven, undriven_2, undriven_3, undriven_4, undriven_5, undriven_6, undriven_7, undriven_8,
       undriven_9, undriven_10, xor_1_out, xor_2_out, xor_3_out, xor_4_out;

  and and_1 (and_1_out, undriven_2, undriven_3);
  xor xor_1 (xor_1_out, undriven_2, undriven_3);
  and and_2 (and_2_out, undriven_4, undriven_5);
  xor xor_2 (xor_2_out, undriven_4, undriven_5);
  and and_3 (and_3_out, undriven_6, undriven_7);
  xor xor_3 (xor_3_out, undriven_6, undriven_7);
  and and_4 (and_4_out, undriven_8, undriven_9);
  xor xor_4 (xor_4_out, undriven_8, undriven_9);
  and and_5 (and_5_out, undriven, and_1_out);
  and and_6 (and_6_out, undriven, and_1_out, undriven_10);
  and and_7 (and_7_out, xor_1_out, and_2_out);
  and and_8 (and_8_out, undriven, and_1_out, undriven_10, and_3_out);
  and and_9 (and_9_out, undriven, undriven_10, and_3_out);
  and and_10 (and_10_out, xor_2_out, and_3_out);
  and and_11 (and_11_out, undriven, and_1_out, undriven_10, and_3_out, and_4_out);
  and and_12 (and_12_out, xor_1_out, undriven_10, and_3_out, and_4_out);
  and and_13 (and_13_out, xor_2_out, and_3_out, and_4_out);
  and and_14 (and_14_out, xor_3_out, and_4_out);
  or or_1 (or_1_out, and_5_out, xor_1_out);
  or or_2 (or_2_out, and_6_out, and_7_out, xor_2_out);
  or or_3 (or_3_out, and_8_out, and_9_out, and_10_out, xor_3_out);
  or or_4 (or_4_out, and_11_out, and_12_out, and_13_out, and_14_out, xor_4_out);
endmodule
